# Fritzing sketch rotary_dial_tester (saved by Fritzing 0.9.3b)
breadboards: 1

parts:
  Part1 = Arduino Uno (Rev3)
  U1 = mystery part, 3 pins [chip_label="Rotary Dila, Siemens standard"]
  LED1 = LED - 5mm [color="Yellow (595nm)" package="5 mm [THT]"]
  LED2 = LED - 5mm [color="Green (570nm)" package="5 mm [THT]"]
  R1 = Resistor [tolerance=±5% resistance=330 package=THT]
  R2 = Resistor [tolerance=±5% resistance=330 package=THT]
  LED3 = LED - 5mm [color="Yellow (595nm)" package="5 mm [THT]"]
  LED4 = LED - 5mm [color="Green (570nm)" package="5 mm [THT]"]
  LED5 = LED - 5mm [color="Yellow (595nm)" package="5 mm [THT]"]
  LED6 = LED - 5mm [color="Green (570nm)" package="5 mm [THT]"]
  LED7 = LED - 5mm [color="Green (570nm)" package="5 mm [THT]"]
  LED8 = LED - 5mm [color="Green (570nm)" package="5 mm [THT]"]
  LED9 = LED - 5mm [color="Green (570nm)" package="5 mm [THT]"]
  LED10 = LED - 5mm [color="Green (570nm)" package="5 mm [THT]"]
  R3 = Resistor [tolerance=±5% resistance=330 package=THT]
  R4 = Resistor [tolerance=±5% resistance=330 package=THT]
  R5 = Resistor [tolerance=±5% resistance=330 package=THT]
  R6 = Resistor [tolerance=±5% resistance=330 package=THT]
  R7 = Resistor [tolerance=±5% resistance=330 package=THT]
  R8 = Resistor [tolerance=±5% resistance=330 package=THT]
  R9 = Resistor [tolerance=±5% resistance=330 package=THT]
  R10 = Resistor [tolerance=±5% resistance=330 package=THT]
  U2 = 74HC595 [package="DIP16 [THT]"]

nets:
  N1: Part1.D2, U1.pin1, R1.Pin_1
  N2: Part1.D3_PWM, U1.pin2, R2.Pin_1
  N3: Part1.D4, U2.DS
  N4: Part1.D5_PWM, U2.ST_CP
  N5: Part1.D6_PWM, U2.SH_CP
  5V: Part1.5V, U1.pin3, U2.MR, U2.VCC
  N6: LED1.cathode, LED2.cathode, LED3.cathode, LED4.cathode, LED5.cathode, LED6.cathode, LED7.cathode, LED8.cathode, LED9.cathode, LED10.cathode, U2.GND, U2.OE
  N7: LED1.anode, R2.Pin_0
  N8: LED2.anode, R1.Pin_0
  N9: LED3.anode, R3.Pin_0
  N10: LED4.anode, R5.Pin_0
  N11: LED5.anode, R4.Pin_0
  N12: LED6.anode, R6.Pin_0
  N13: LED7.anode, R7.Pin_0
  N14: LED8.anode, R8.Pin_0
  N15: LED9.anode, R9.Pin_0
  N16: LED10.anode, R10.Pin_0
  N17: R3.Pin_1, U2.Q0
  N18: R4.Pin_1, U2.Q1
  N19: R5.Pin_1, U2.Q2
  N20: R6.Pin_1, U2.Q3
  N21: R7.Pin_1, U2.Q4
  N22: R8.Pin_1, U2.Q5
  N23: R9.Pin_1, U2.Q6
  N24: R10.Pin_1, U2.Q7
